# Fritzing sketch diagram (saved by Fritzing 0.9.6b)
breadboards: 1

parts:
  19957_SparkFun_AzureWave_Thing_Plus_AW-CU1 = SparkFun AzureWave Thing Plus (AW-CU488) [part_number=DEV-19957]
  19389_SparkFun_Analog_MEMS_Microphone_Breakout_-_SPH8878LR5H-2 = SparkFun Analog MEMS Microphone Breakout - SPH8878LR5H-1 [part_number=19389]

nets:
  GND: 19957_SparkFun_AzureWave_Thing_Plus_AW-CU1.GND, 19389_SparkFun_Analog_MEMS_Microphone_Breakout_-_SPH8878LR5H-2.GND
  3.3V: 19957_SparkFun_AzureWave_Thing_Plus_AW-CU1.3.3V, 19389_SparkFun_Analog_MEMS_Microphone_Breakout_-_SPH8878LR5H-2.VCC
  N1: 19957_SparkFun_AzureWave_Thing_Plus_AW-CU1.22_(PA4), 19389_SparkFun_Analog_MEMS_Microphone_Breakout_-_SPH8878LR5H-2.AUD

custom parts:
  SparkFun AzureWave Thing Plus (AW-CU488): The SparkFun AzureWave Thing Plus is a Feather form-factor development board equipped with the AW-CU488. The module features the Realtek RTL8721DM integrated single-chip low power dual band (2.4GHz and 5GHz) wireless LAN and Bluetooth&reg; Low Energy (V5.0) communication controller. Connect the SparkFun AzureWave Thing Plus to the cloud to grab current weather conditions in your area, post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
  SparkFun Analog MEMS Microphone Breakout - SPH8878LR5H-1: The SparkFun Analog MEMS Microphone Breakout makes it easy to work with the SPH8878LR5H-1 analog microphone from Knowles. This board features an OpAmp to bring the output of the microphone to a usable level, allowing you to plug directly into an ADC on a microcontroller or something like the [SparkFun Spectrum Shield](https://www.sparkfun.com/products/13116). In addition to amplifying the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
